// Logisim project trabalho.circ as structural Verilog: 30 circuits, main circuit Somador1bit
module main (
  input  in_1,
  output [31:0] out_2,
  output [31:0] out_3
);

  wire clk, Display, ehZero, JouZ, Jump, multiplexer_1_out, SelCONST, We;
  wire [2:0] SelULA;
  wire [31:0] bancoderegistradores_1_saidaa, bancoderegistradores_1_saidab, bit_extender_1_out,
       bit_extender_2_out, multiplexer_2_out, multiplexer_3_out, register_1_q, rom_1_data, somador_1_r,
       ula_1_saida;

  Multiplexer multiplexer_1 (.in0(Jump), .in1(ehZero), .out(multiplexer_1_out), .sel(JouZ));
  Multiplexer #(.width(32)) multiplexer_2 (
    .in0(32'h1), .in1(bit_extender_1_out), .out(multiplexer_2_out), .sel(multiplexer_1_out));
  assign bit_extender_1_out = {{16{rom_1_data[31]}}, rom_1_data[31:16]};  // Bit_Extender bit_extender_1
  Somador somador_1 (
    .R(somador_1_r), .A({register_1_q[31:26], register_1_q[31:26], register_1_q[31:26], register_1_q[13:0]}),
    .B(multiplexer_2_out), .sub(1'b0));
  Register #(.width(32)) register_1 (
    .D(somador_1_r), .en(1'b1), .clk(clk),
    .Q({register_1_q[31:26], register_1_q[31:26], register_1_q[31:26], register_1_q[13:0]}), .clr(in_1));
  ROM #(.addrWidth(7), .dataWidth(32)) rom_1 (.addr(register_1_q[6:0]), .data(rom_1_data));
  Clock clock_1 (.out(clk));
  MemControle memcontrole_1 (
    .B_ou_CONST(SelCONST), .We(We), .Enb_Display(Display), .Jump(Jump), .jumpOUzero(JouZ), .SelULA(SelULA),
    .in_1(rom_1_data[3:0]));
  assign bit_extender_2_out = {{16{1'b0}}, rom_1_data[31:16]};  // Bit_Extender bit_extender_2
  BancoDeRegistradores bancoderegistradores_1 (
    .SaidaA(bancoderegistradores_1_saidaa), .SaidaB(bancoderegistradores_1_saidab), .a(rom_1_data[7:4]),
    .DadoEscrita(ula_1_saida), .b(rom_1_data[11:8]), .clear(in_1), .c(rom_1_data[15:12]), .clk(clk), .We(We));
  Multiplexer #(.width(32)) multiplexer_3 (
    .in0(bancoderegistradores_1_saidab), .in1(bit_extender_2_out), .out(multiplexer_3_out), .sel(SelCONST));
  Register #(.width(32)) register_2 (.D(bancoderegistradores_1_saidaa), .en(Display), .clk(clk), .Q(out_2), .clr(in_1));
  ULA ula_1 (
    .Saida(ula_1_saida), .ZERO(ehZero), .B(multiplexer_3_out), .A(bancoderegistradores_1_saidaa),
    .Seletor(SelULA));

  assign out_3 = out_2;
  // also tied to GND on the sheet: {register_1_q[7], register_1_q[8], register_1_q[9], register_1_q[10], register_1_q[11], register_1_q[12], register_1_q[13], register_1_q[26], register_1_q[27], register_1_q[28], register_1_q[29], register_1_q[30], register_1_q[31]}

  // Other names for the same wires on the sheet: clear = in_1

  // Notes on the sheet:
  //   contents of rom_1 (hex, n*v repeats v):
  //   5100b 3200b 0 3211 3c 4212 4c 5213 5c 6124 6c 7165 7c 8066 8c 9257 9c 9298 9c 1a039 ac 3d06a dc
  //   9e08b ec 28000d 8*0 1003 8700b a00b 1b00b c003 c0b4 bba1 a003 a0c4 cc 1101b 2017e fff8000d f 0 0
  //   5003 1100b 5c 5591 2052e fffd000d 5c 5952 2050e fffd000d 5c 3012e 1101b fff6000d ffe2000d 20f00b
  //   a00b 1c00b cc cac7 1a0ab cc 20afe fffa000d 0 d00b a0cb c0ab cc cdc8 0 1d0db cc 20dfe fff9000d
  //   ffdd000d
  //   R1 -> 5  0101
  //   R2 -> 3  0011
  //   R3 -> 8  1000
  //   R4 -> 2  0010
  //   R5 -> 1  0001
  //   R6 -> 7  0111
  //   R7 -> 2  0010
  //   R8 -> -8 1000
  //   R9 -> 8-1 1000/ 0001
  //   Ra -> 9 1001
endmodule

module MemControle (
  input  [3:0] in_1,
  output [2:0] SelULA,
  output B_ou_CONST,
  output We,
  output Enb_Display,
  output Jump,
  output jumpOUzero
);

  ROM #(.addrWidth(4)) rom_1 (.addr(in_1), .data({jumpOUzero, Jump, Enb_Display, We, B_ou_CONST, SelULA}));

  // Notes on the sheet:
  //   contents of rom_1 (hex, n*v repeats v):
  //   0 10 11 12 13 14 15 16 17 1b 1c 18 20 40 81 40
  //   00 10 11 12 13 14 15 16
  //   17 1b 1c 18 20 40 81 40
endmodule

module BancoDeRegistradores (
  input  clk,
  input  clear,
  input  [3:0] a,
  input  [3:0] b,
  input  [31:0] DadoEscrita,
  input  We,
  input  [3:0] c,
  output [31:0] SaidaA,
  output [31:0] SaidaB
);

  wire w1, w2, w3, w4, w5, w6, w7, w8, w9, w10, w11, w12, w13, w14, w15, w16;
  wire [31:0] Escre1, Escre2, Escre3, Escre4, Escre5, Escre6, Escre7, Escre8, Escre9, Escre10, Escre11,
       Escre12, Escre13, Escre14, Escre15, Escre16, Tun1, Tun2, Tun3, Tun4, Tun5, Tun6, Tun7, Tun8, Tun9,
       Tun10, Tun11, Tun12, Tun13, Tun14, Tun15, Tun16;

  Multiplexer #(.select(4), .width(32)) multiplexer_1 (
    .in0(Tun1), .in1(Tun2), .in2(Tun3), .in3(Tun4), .in4(Tun5), .in5(Tun6), .in6(Tun7), .in7(Tun8),
    .in8(Tun9), .in9(Tun10), .in10(Tun11), .in11(Tun12), .in12(Tun13), .in13(Tun14), .in14(Tun15),
    .in15(Tun16), .out(SaidaA), .sel(a));
  Demultiplexer #(.select(4), .width(32)) demultiplexer_1 (
    .out0(Escre1), .out1(Escre2), .out2(Escre3), .out3(Escre4), .out4(Escre5), .out5(Escre6), .out6(Escre7),
    .out7(Escre8), .out8(Escre9), .out9(Escre10), .out10(Escre11), .out11(Escre12), .out12(Escre13),
    .out13(Escre14), .out14(Escre15), .out15(Escre16), .in(DadoEscrita), .sel(c));
  Multiplexer #(.select(4), .width(32)) multiplexer_2 (
    .in0(Tun1), .in1(Tun2), .in2(Tun3), .in3(Tun4), .in4(Tun5), .in5(Tun6), .in6(Tun7), .in7(Tun8),
    .in8(Tun9), .in9(Tun10), .in10(Tun11), .in11(Tun12), .in12(Tun13), .in13(Tun14), .in14(Tun15),
    .in15(Tun16), .out(SaidaB), .sel(b));
  Register #(.width(32)) R1 (.D(Escre1), .en(w1), .clk(clk), .Q(Tun1), .clr(1'b1));
  Register #(.width(32)) R5 (.D(Escre5), .en(w5), .clk(clk), .Q(Tun5), .clr(clear));
  Register #(.width(32)) R9 (.D(Escre9), .en(w9), .clk(clk), .Q(Tun9), .clr(clear));
  Register #(.width(32)) R13 (.D(Escre13), .en(w13), .clk(clk), .Q(Tun13), .clr(clear));
  Demultiplexer #(.select(4)) demultiplexer_2 (
    .out0(w1), .out1(w2), .out2(w3), .out3(w4), .out4(w5), .out5(w6), .out6(w7), .out7(w8), .out8(w9),
    .out9(w10), .out10(w11), .out11(w12), .out12(w13), .out13(w14), .out14(w15), .out15(w16), .in(We), .sel(c));
  Register #(.width(32)) R2 (.D(Escre2), .en(w2), .clk(clk), .Q(Tun2), .clr(clear));
  Register #(.width(32)) R6 (.D(Escre6), .en(w6), .clk(clk), .Q(Tun6), .clr(clear));
  Register #(.width(32)) R10 (.D(Escre10), .en(w10), .clk(clk), .Q(Tun10), .clr(clear));
  Register #(.width(32)) R14 (.D(Escre14), .en(w14), .clk(clk), .Q(Tun14), .clr(clear));
  Register #(.width(32)) R3 (.D(Escre3), .en(w3), .clk(clk), .Q(Tun3), .clr(clear));
  Register #(.width(32)) R7 (.D(Escre7), .en(w7), .clk(clk), .Q(Tun7), .clr(clear));
  Register #(.width(32)) R11 (.D(Escre11), .en(w11), .clk(clk), .Q(Tun11), .clr(clear));
  Register #(.width(32)) R15 (.D(Escre15), .en(w15), .clk(clk), .Q(Tun15), .clr(clear));
  Register #(.width(32)) R4 (.D(Escre4), .en(w4), .clk(clk), .Q(Tun4), .clr(clear));
  Register #(.width(32)) R8 (.D(Escre8), .en(w8), .clk(clk), .Q(Tun8), .clr(clear));
  Register #(.width(32)) R12 (.D(Escre12), .en(w12), .clk(clk), .Q(Tun12), .clr(clear));
  Register #(.width(32)) R16 (.D(Escre16), .en(w16), .clk(clk), .Q(Tun16), .clr(clear));

  // Other names for the same wires on the sheet: cle = clear

  // Notes on the sheet:
  //   Túneis do Escre
endmodule

module ULA (
  input  [31:0] A,
  input  [31:0] B,
  input  [2:0] Seletor,
  output ZERO,
  output [31:0] Saida
);

  wire auxshift_1_saida;
  wire [31:0] And32_out, NotA32_out, Or32_out, shiftdir_1_resultado, shifteresq_1_saida, somador_1_r,
       somador_2_r, Xor32_out;

  Somador somador_1 (.R(somador_1_r), .A(A), .B(B), .sub(1'b0));
  Somador somador_2 (.R(somador_2_r), .A(A), .B(B), .sub(1'b1));
  assign And32_out = A & B;  // AND_Gate And32, 32 bits wide
  assign Or32_out = A | B;  // OR_Gate Or32, 32 bits wide
  Multiplexer #(.select(3), .width(32)) multiplexer_1 (
    .in0(somador_1_r), .in1(somador_2_r), .in2(And32_out), .in3(Or32_out), .in4(Xor32_out), .in5(NotA32_out),
    .in6(shifteresq_1_saida), .in7(shiftdir_1_resultado), .out(Saida), .sel(Seletor));
  assign Xor32_out = A ^ B;  // XOR_Gate Xor32, 32 bits wide
  AuxSHIFT auxshift_1 (
    .saida(auxshift_1_saida), .in40(Saida[23:20]), .in41(Saida[27:24]), .in42(Saida[31:28]),
    .in52(Saida[19:15]), .in50(Saida[9:5]), .in51(Saida[14:10]));
  assign NotA32_out = ~A;  // NOT_Gate NotA32, 32 bits wide
  nor nor_1 (ZERO, Saida[0], Saida[1], Saida[2], Saida[3], Saida[4], auxshift_1_saida);
  ShifterESQ shifteresq_1 (.Saida(shifteresq_1_saida), .seletor(B), .Entrada(A));
  ShiftDIR shiftdir_1 (.resultado(shiftdir_1_resultado), .B(B), .A(A));
endmodule

module Somador (
  input  [31:0] A,
  input  [31:0] B,
  input  sub,
  output [31:0] R
);

  wire lacomcs4bits_1_cout, lacomcs4bits_2_cout, lacomcs4bits_3_cout, lacomcs4bits_4_cout,
       lacomcs4bits_5_cout, lacomcs4bits_6_cout, lookahead4bits_1_cout;
  wire [3:0] multiplexer_1_out, multiplexer_1_out_2, multiplexer_1_out_3, multiplexer_1_out_4,
       multiplexer_1_out_5, multiplexer_1_out_6, multiplexer_1_out_7, multiplexer_1_out_8;
  wire [31:0] not_1_out;

  assign not_1_out = ~B;  // NOT_Gate not_1, 32 bits wide
  Multiplexer #(.width(32)) multiplexer_1 (
    .in0(B), .in1(not_1_out),
    .out({multiplexer_1_out_8, multiplexer_1_out_7, multiplexer_1_out_6, multiplexer_1_out_5, multiplexer_1_out_4, multiplexer_1_out_3, multiplexer_1_out_2, multiplexer_1_out}),
    .sel(sub));
  LookAhead4bits lookahead4bits_1 (
    .Cout(lookahead4bits_1_cout), .out_5(R[3:0]), .B(multiplexer_1_out), .A(A[3:0]), .Cin(sub));
  LAcomCS4bits lacomcs4bits_1 (
    .Cout(lacomcs4bits_1_cout), .R(R[7:4]), .Csel(lookahead4bits_1_cout), .A(A[7:4]), .B(multiplexer_1_out_2));
  LAcomCS4bits lacomcs4bits_2 (
    .Cout(lacomcs4bits_2_cout), .R(R[11:8]), .Csel(lacomcs4bits_1_cout), .A(A[11:8]), .B(multiplexer_1_out_3));
  LAcomCS4bits lacomcs4bits_3 (
    .Cout(lacomcs4bits_3_cout), .R(R[15:12]), .Csel(lacomcs4bits_2_cout), .A(A[15:12]),
    .B(multiplexer_1_out_4));
  LAcomCS4bits lacomcs4bits_4 (
    .Cout(lacomcs4bits_4_cout), .R(R[19:16]), .Csel(lacomcs4bits_3_cout), .A(A[19:16]),
    .B(multiplexer_1_out_5));
  LAcomCS4bits lacomcs4bits_5 (
    .Cout(lacomcs4bits_5_cout), .R(R[23:20]), .Csel(lacomcs4bits_4_cout), .A(A[23:20]),
    .B(multiplexer_1_out_6));
  LAcomCS4bits lacomcs4bits_6 (
    .Cout(lacomcs4bits_6_cout), .R(R[27:24]), .Csel(lacomcs4bits_5_cout), .A(A[27:24]),
    .B(multiplexer_1_out_7));
  LAcomCS4bits lacomcs4bits_7 (
    .R(R[31:28]), .Csel(lacomcs4bits_6_cout), .A(A[31:28]), .B(multiplexer_1_out_8));  // open: Cout

  // Notes on the sheet:
  //   A: pull=down
  //   B: pull=down
endmodule

module ShifterESQ (
  input  [31:0] Entrada,
  input  [31:0] seletor,
  output [31:0] Saida
);

  wire auxshift_1_saida;
  wire [31:0] shifesq1_1_saida, shiftesq2_1_saida, shiftesq4_1_saida, shiftesq8_1_saida, shiftesq16_1_saida;

  AuxSHIFT auxshift_1 (
    .saida(auxshift_1_saida), .in40(seletor[23:20]), .in41(seletor[27:24]), .in42(seletor[31:28]),
    .in52(seletor[19:15]), .in50(seletor[9:5]), .in51(seletor[14:10]));
  ShifESQ1 shifesq1_1 (.saida(shifesq1_1_saida), .Entrada(Entrada), .Seletor(seletor[0]));
  ShiftESQ2 shiftesq2_1 (.saida(shiftesq2_1_saida), .entrada(shifesq1_1_saida), .sel(seletor[1]));
  Multiplexer #(.width(32)) multiplexer_1 (
    .in0(shiftesq16_1_saida), .in1({32{1'b0}}), .out(Saida), .sel(auxshift_1_saida));
  ShiftESQ4 shiftesq4_1 (.saida(shiftesq4_1_saida), .entrada(shiftesq2_1_saida), .seletor(seletor[2]));
  ShiftESQ8 shiftesq8_1 (.saida(shiftesq8_1_saida), .entrad(shiftesq4_1_saida), .seletor(seletor[3]));
  ShiftESQ16 shiftesq16_1 (.saida(shiftesq16_1_saida), .entrada(shiftesq8_1_saida), .seletor(seletor[4]));
endmodule

module ShiftDIR (
  input  [31:0] A,
  input  [31:0] B,
  output [31:0] resultado
);

  wire auxshift_1_saida;
  wire [31:0] shiftdir1_1_out_3, shiftdir2_1_out_3, shiftdir4_1_out_3, shiftdir8_1_out_3, shiftdir16_1_out_3;

  AuxSHIFT auxshift_1 (
    .saida(auxshift_1_saida), .in40(B[23:20]), .in41(B[27:24]), .in42(B[31:28]), .in52(B[19:15]),
    .in50(B[9:5]), .in51(B[14:10]));
  ShiftDIR1 shiftdir1_1 (.out_3(shiftdir1_1_out_3), .in_2(A), .in_1(B[0]));
  Multiplexer #(.width(32)) multiplexer_1 (
    .in0(shiftdir16_1_out_3), .in1({32{1'b0}}), .out(resultado), .sel(auxshift_1_saida));
  ShiftDIR2 shiftdir2_1 (.out_3(shiftdir2_1_out_3), .in_2(shiftdir1_1_out_3), .in_1(B[1]));
  ShiftDIR4 shiftdir4_1 (.out_3(shiftdir4_1_out_3), .inn(shiftdir2_1_out_3), .sel(B[2]));
  ShiftDIR8 shiftdir8_1 (.out_3(shiftdir8_1_out_3), .inn(shiftdir4_1_out_3), .sel(B[3]));
  ShiftDIR16 shiftdir16_1 (.out_3(shiftdir16_1_out_3), .inn(shiftdir8_1_out_3), .sel(B[4]));
endmodule

module AuxSHIFT (
  input  [4:0] in50,
  input  [4:0] in51,
  input  [4:0] in52,
  input  [3:0] in40,
  input  [3:0] in41,
  input  [3:0] in42,
  output saida
);

  wire or_1_out, or_2_out, or_3_out, or_4_out, or_5_out, or_6_out;

  or or_1 (or_1_out, in50[0], in50[1], in50[2], in50[3], in50[4]);
  or or_2 (or_2_out, in51[0], in51[1], in51[2], in51[3], in51[4]);
  or or_3 (or_3_out, in52[0], in52[1], in52[2], in52[3], in52[4]);
  or or_4 (or_4_out, in40[0], in40[1], in40[2], in40[3]);
  or or_5 (or_5_out, in41[0], in41[1], in41[2], in41[3]);
  or or_6 (or_6_out, in42[0], in42[1], in42[2], in42[3]);
  or or_7 (saida, or_1_out, or_2_out, or_3_out, or_4_out, or_5_out, or_6_out);
endmodule

module SE41 (
  input  Constante,
  input  [3:0] Entrada,
  input  Seletor,
  output DadoAnter,
  output [3:0] Saida
);

  Multiplexer multiplexer_1 (.in0(Entrada[3]), .in1(Entrada[2]), .out(Saida[3]), .sel(Seletor));
  Multiplexer multiplexer_2 (.in0(Entrada[2]), .in1(Entrada[1]), .out(Saida[2]), .sel(Seletor));
  Multiplexer multiplexer_3 (.in0(Entrada[1]), .in1(Entrada[0]), .out(Saida[1]), .sel(Seletor));
  Multiplexer multiplexer_4 (.in0(Entrada[0]), .in1(Constante), .out(Saida[0]), .sel(Seletor));

  assign DadoAnter = Entrada[3];
endmodule

module ShifESQ1 (
  input  Seletor,
  input  [31:0] Entrada,
  output [31:0] saida
);

  wire se41_1_dadoanter, se41_2_dadoanter, se41_3_dadoanter, se41_4_dadoanter, se41_5_dadoanter,
       se41_6_dadoanter, se41_7_dadoanter;

  SE41 se41_1 (
    .DadoAnter(se41_1_dadoanter), .Saida(saida[3:0]), .Entrada(Entrada[3:0]), .Constante(1'b0),
    .Seletor(Seletor));
  SE41 se41_2 (
    .DadoAnter(se41_2_dadoanter), .Saida(saida[7:4]), .Entrada(Entrada[7:4]), .Constante(se41_1_dadoanter),
    .Seletor(Seletor));
  SE41 se41_3 (
    .DadoAnter(se41_3_dadoanter), .Saida(saida[11:8]), .Entrada(Entrada[11:8]), .Constante(se41_2_dadoanter),
    .Seletor(Seletor));
  SE41 se41_4 (
    .DadoAnter(se41_4_dadoanter), .Saida(saida[15:12]), .Entrada(Entrada[15:12]),
    .Constante(se41_3_dadoanter), .Seletor(Seletor));
  SE41 se41_5 (
    .DadoAnter(se41_5_dadoanter), .Saida(saida[19:16]), .Entrada(Entrada[19:16]),
    .Constante(se41_4_dadoanter), .Seletor(Seletor));
  SE41 se41_6 (
    .DadoAnter(se41_6_dadoanter), .Saida(saida[23:20]), .Entrada(Entrada[23:20]),
    .Constante(se41_5_dadoanter), .Seletor(Seletor));
  SE41 se41_7 (
    .DadoAnter(se41_7_dadoanter), .Saida(saida[27:24]), .Entrada(Entrada[27:24]),
    .Constante(se41_6_dadoanter), .Seletor(Seletor));
  SE41 se41_8 (
    .Saida(saida[31:28]), .Entrada(Entrada[31:28]), .Constante(se41_7_dadoanter), .Seletor(Seletor));  // open: DadoAnter
endmodule

module SE42 (
  input  [3:0] entrada,
  input  MSE,
  input  LSE,
  input  sel,
  output MS,
  output LS,
  output [3:0] saida
);

  Multiplexer multiplexer_1 (.in0(entrada[3]), .in1(entrada[1]), .out(saida[3]), .sel(sel));
  Multiplexer multiplexer_2 (.in0(entrada[2]), .in1(entrada[0]), .out(saida[2]), .sel(sel));
  Multiplexer multiplexer_3 (.in0(entrada[1]), .in1(MSE), .out(saida[1]), .sel(sel));
  Multiplexer multiplexer_4 (.in0(entrada[0]), .in1(LSE), .out(saida[0]), .sel(sel));

  assign LS = entrada[2];
  assign MS = entrada[3];
endmodule

module ShiftESQ2 (
  input  sel,
  input  [31:0] entrada,
  output [31:0] saida
);

  wire se42_1_ls, se42_1_ms, se42_2_ls, se42_2_ms, se42_3_ls, se42_3_ms, se42_4_ls, se42_4_ms, se42_5_ls,
       se42_5_ms, se42_6_ls, se42_6_ms, se42_7_ls, se42_7_ms;

  SE42 se42_1 (
    .MS(se42_1_ms), .saida(saida[3:0]), .LS(se42_1_ls), .entrada(entrada[3:0]), .MSE(1'b0), .LSE(1'b0),
    .sel(sel));
  SE42 se42_2 (
    .MS(se42_2_ms), .saida(saida[7:4]), .LS(se42_2_ls), .entrada(entrada[7:4]), .MSE(se42_1_ms),
    .LSE(se42_1_ls), .sel(sel));
  SE42 se42_3 (
    .MS(se42_3_ms), .saida(saida[11:8]), .LS(se42_3_ls), .entrada(entrada[11:8]), .MSE(se42_2_ms),
    .LSE(se42_2_ls), .sel(sel));
  SE42 se42_4 (
    .MS(se42_4_ms), .saida(saida[15:12]), .LS(se42_4_ls), .entrada(entrada[15:12]), .MSE(se42_3_ms),
    .LSE(se42_3_ls), .sel(sel));
  SE42 se42_5 (
    .MS(se42_5_ms), .saida(saida[19:16]), .LS(se42_5_ls), .entrada(entrada[19:16]), .MSE(se42_4_ms),
    .LSE(se42_4_ls), .sel(sel));
  SE42 se42_6 (
    .MS(se42_6_ms), .saida(saida[23:20]), .LS(se42_6_ls), .entrada(entrada[23:20]), .MSE(se42_5_ms),
    .LSE(se42_5_ls), .sel(sel));
  SE42 se42_7 (
    .MS(se42_7_ms), .saida(saida[27:24]), .LS(se42_7_ls), .entrada(entrada[27:24]), .MSE(se42_6_ms),
    .LSE(se42_6_ls), .sel(sel));
  SE42 se42_8 (
    .saida(saida[31:28]), .entrada(entrada[31:28]), .MSE(se42_7_ms), .LSE(se42_7_ls), .sel(sel));  // open: MS, LS
endmodule

module SE84 (
  input  ms,
  input  dois,
  input  um,
  input  ls,
  input  [7:0] Entrada,
  input  sel,
  output mss,
  output ds,
  output ums,
  output lss,
  output [7:0] Saida
);

  Multiplexer multiplexer_1 (.in0(Entrada[6]), .in1(Entrada[2]), .out(Saida[6]), .sel(sel));
  Multiplexer multiplexer_2 (.in0(Entrada[7]), .in1(Entrada[3]), .out(Saida[7]), .sel(sel));
  Multiplexer multiplexer_3 (.in0(Entrada[5]), .in1(Entrada[1]), .out(Saida[5]), .sel(sel));
  Multiplexer multiplexer_4 (.in0(Entrada[3]), .in1(ms), .out(Saida[3]), .sel(sel));
  Multiplexer multiplexer_5 (.in0(Entrada[4]), .in1(Entrada[0]), .out(Saida[4]), .sel(sel));
  Multiplexer multiplexer_6 (.in0(Entrada[2]), .in1(dois), .out(Saida[2]), .sel(sel));
  Multiplexer multiplexer_7 (.in0(Entrada[0]), .in1(ls), .out(Saida[0]), .sel(sel));
  Multiplexer multiplexer_8 (.in0(Entrada[1]), .in1(um), .out(Saida[1]), .sel(sel));

  assign ds = Entrada[6];
  assign lss = Entrada[4];
  assign mss = Entrada[7];
  assign ums = Entrada[5];
endmodule

module ShiftESQ4 (
  input  seletor,
  input  [31:0] entrada,
  output [31:0] saida
);

  wire se84_1_ds, se84_1_lss, se84_1_mss, se84_1_ums, se84_2_ds, se84_2_lss, se84_2_mss, se84_2_ums,
       se84_3_ds, se84_3_lss, se84_3_mss, se84_3_ums;

  SE84 se84_1 (
    .lss(se84_1_lss), .mss(se84_1_mss), .ds(se84_1_ds), .Saida(saida[7:0]), .ums(se84_1_ums),
    .Entrada(entrada[7:0]), .ms(1'b0), .dois(1'b0), .um(1'b0), .ls(1'b0), .sel(seletor));
  SE84 se84_2 (
    .lss(se84_2_lss), .mss(se84_2_mss), .ds(se84_2_ds), .Saida(saida[15:8]), .ums(se84_2_ums),
    .Entrada(entrada[15:8]), .ms(se84_1_mss), .dois(se84_1_ds), .um(se84_1_ums), .ls(se84_1_lss),
    .sel(seletor));
  SE84 se84_3 (
    .lss(se84_3_lss), .mss(se84_3_mss), .ds(se84_3_ds), .Saida(saida[23:16]), .ums(se84_3_ums),
    .Entrada(entrada[23:16]), .ms(se84_2_mss), .dois(se84_2_ds), .um(se84_2_ums), .ls(se84_2_lss),
    .sel(seletor));
  SE84 se84_4 (
    .Saida(saida[31:24]), .Entrada(entrada[31:24]), .ms(se84_3_mss), .dois(se84_3_ds), .um(se84_3_ums),
    .ls(se84_3_lss), .sel(seletor));  // open: lss, mss, ds, ums
endmodule

module SE168 (
  input  [15:0] entrada,
  input  da1,
  input  da2,
  input  da3,
  input  da4,
  input  da5,
  input  da6,
  input  da7,
  input  da8,
  input  sel,
  output s1,
  output s2,
  output s3,
  output s4,
  output s5,
  output s6,
  output s7,
  output s8,
  output [15:0] out_19
);

  Multiplexer multiplexer_1 (.in0(entrada[15]), .in1(entrada[7]), .out(out_19[15]), .sel(sel));
  Multiplexer multiplexer_2 (.in0(entrada[14]), .in1(entrada[6]), .out(out_19[14]), .sel(sel));
  Multiplexer multiplexer_3 (.in0(entrada[13]), .in1(entrada[5]), .out(out_19[13]), .sel(sel));
  Multiplexer multiplexer_4 (.in0(entrada[12]), .in1(entrada[4]), .out(out_19[12]), .sel(sel));
  Multiplexer multiplexer_5 (.in0(entrada[11]), .in1(entrada[3]), .out(out_19[11]), .sel(sel));
  Multiplexer multiplexer_6 (.in0(entrada[10]), .in1(entrada[2]), .out(out_19[10]), .sel(sel));
  Multiplexer multiplexer_7 (.in0(entrada[9]), .in1(entrada[1]), .out(out_19[9]), .sel(sel));
  Multiplexer multiplexer_8 (.in0(entrada[8]), .in1(entrada[0]), .out(out_19[8]), .sel(sel));
  Multiplexer multiplexer_9 (.in0(entrada[7]), .in1(da1), .out(out_19[7]), .sel(sel));
  Multiplexer multiplexer_10 (.in0(entrada[6]), .in1(da2), .out(out_19[6]), .sel(sel));
  Multiplexer multiplexer_11 (.in0(entrada[5]), .in1(da3), .out(out_19[5]), .sel(sel));
  Multiplexer multiplexer_12 (.in0(entrada[4]), .in1(da4), .out(out_19[4]), .sel(sel));
  Multiplexer multiplexer_13 (.in0(entrada[3]), .in1(da5), .out(out_19[3]), .sel(sel));
  Multiplexer multiplexer_14 (.in0(entrada[2]), .in1(da6), .out(out_19[2]), .sel(sel));
  Multiplexer multiplexer_15 (.in0(entrada[1]), .in1(da7), .out(out_19[1]), .sel(sel));
  Multiplexer multiplexer_16 (.in0(entrada[0]), .in1(da8), .out(out_19[0]), .sel(sel));

  assign s1 = entrada[15];
  assign s2 = entrada[14];
  assign s3 = entrada[13];
  assign s4 = entrada[12];
  assign s5 = entrada[11];
  assign s6 = entrada[10];
  assign s7 = entrada[9];
  assign s8 = entrada[8];
endmodule

module ShiftESQ8 (
  input  seletor,
  input  [31:0] entrad,
  output [31:0] saida
);

  wire se168_1_s1, se168_1_s2, se168_1_s3, se168_1_s4, se168_1_s5, se168_1_s6, se168_1_s7, se168_1_s8;

  SE168 se168_1 (
    .s1(se168_1_s1), .s2(se168_1_s2), .out_19(saida[15:0]), .s3(se168_1_s3), .s4(se168_1_s4),
    .s5(se168_1_s5), .s6(se168_1_s6), .s7(se168_1_s7), .s8(se168_1_s8), .sel(seletor), .da1(1'b0),
    .da2(1'b0), .da3(1'b0), .da4(1'b0), .da5(1'b0), .da6(1'b0), .da7(1'b0), .da8(1'b0), .entrada(entrad[15:0]));
  SE168 se168_2 (
    .out_19(saida[31:16]), .sel(seletor), .da1(se168_1_s1), .da2(se168_1_s2), .da3(se168_1_s3),
    .da4(se168_1_s4), .da5(se168_1_s5), .da6(se168_1_s6), .da7(se168_1_s7), .da8(se168_1_s8),
    .entrada(entrad[31:16]));  // open: s1, s2, s3, s4, s5, s6, s7, s8
endmodule

module ShiftESQ16 (
  input  seletor,
  input  [31:0] entrada,
  output [31:0] saida
);

  wire [31:0] shiftesq8_1_saida;

  ShiftESQ8 shiftesq8_1 (.saida(shiftesq8_1_saida), .entrad(entrada), .seletor(seletor));
  ShiftESQ8 shiftesq8_2 (.saida(saida), .entrad(shiftesq8_1_saida), .seletor(seletor));
endmodule

module SD41 (
  input  [3:0] entrada,
  input  Const,
  input  seletor,
  output DadoAnter,
  output [3:0] saida
);

  Multiplexer multiplexer_1 (.in0(entrada[3]), .in1(Const), .out(saida[3]), .sel(seletor));
  Multiplexer multiplexer_2 (.in0(entrada[2]), .in1(entrada[3]), .out(saida[2]), .sel(seletor));
  Multiplexer multiplexer_3 (.in0(entrada[1]), .in1(entrada[2]), .out(saida[1]), .sel(seletor));
  Multiplexer multiplexer_4 (.in0(entrada[0]), .in1(entrada[1]), .out(saida[0]), .sel(seletor));

  assign DadoAnter = entrada[0];
endmodule

module ShiftDIR1 (
  input  in_1,
  input  [31:0] in_2,
  output [31:0] out_3
);

  wire sd41_2_dadoanter, sd41_3_dadoanter, sd41_4_dadoanter, sd41_5_dadoanter, sd41_6_dadoanter,
       sd41_7_dadoanter, sd41_8_dadoanter;

  SD41 sd41_1 (.saida(out_3[3:0]), .seletor(in_1), .Const(sd41_2_dadoanter), .entrada(in_2[3:0]));  // open: DadoAnter
  SD41 sd41_2 (
    .saida(out_3[7:4]), .DadoAnter(sd41_2_dadoanter), .seletor(in_1), .Const(sd41_3_dadoanter),
    .entrada(in_2[7:4]));
  SD41 sd41_3 (
    .saida(out_3[11:8]), .DadoAnter(sd41_3_dadoanter), .seletor(in_1), .Const(sd41_4_dadoanter),
    .entrada(in_2[11:8]));
  SD41 sd41_4 (
    .saida(out_3[15:12]), .DadoAnter(sd41_4_dadoanter), .seletor(in_1), .Const(sd41_5_dadoanter),
    .entrada(in_2[15:12]));
  SD41 sd41_5 (
    .saida(out_3[19:16]), .DadoAnter(sd41_5_dadoanter), .seletor(in_1), .Const(sd41_6_dadoanter),
    .entrada(in_2[19:16]));
  SD41 sd41_6 (
    .saida(out_3[23:20]), .DadoAnter(sd41_6_dadoanter), .seletor(in_1), .Const(sd41_7_dadoanter),
    .entrada(in_2[23:20]));
  SD41 sd41_7 (
    .saida(out_3[27:24]), .DadoAnter(sd41_7_dadoanter), .seletor(in_1), .Const(sd41_8_dadoanter),
    .entrada(in_2[27:24]));
  SD41 sd41_8 (.saida(out_3[31:28]), .DadoAnter(sd41_8_dadoanter), .seletor(in_1), .Const(1'b0), .entrada(in_2[31:28]));
endmodule

module SD42 (
  input  [3:0] entrada,
  input  ms,
  input  ls,
  input  sel,
  output mss,
  output lss,
  output [3:0] saida
);

  Multiplexer multiplexer_1 (.in0(entrada[3]), .in1(ms), .out(saida[3]), .sel(sel));
  Multiplexer multiplexer_2 (.in0(entrada[2]), .in1(ls), .out(saida[2]), .sel(sel));
  Multiplexer multiplexer_3 (.in0(entrada[1]), .in1(entrada[3]), .out(saida[1]), .sel(sel));
  Multiplexer multiplexer_4 (.in0(entrada[0]), .in1(entrada[2]), .out(saida[0]), .sel(sel));

  assign lss = entrada[0];
  assign mss = entrada[1];
endmodule

module ShiftDIR2 (
  input  in_1,
  input  [31:0] in_2,
  output [31:0] out_3
);

  wire sd42_2_lss, sd42_2_mss, sd42_3_lss, sd42_3_mss, sd42_4_lss, sd42_4_mss, sd42_5_lss, sd42_5_mss,
       sd42_6_lss, sd42_6_mss, sd42_7_lss, sd42_7_mss, sd42_8_lss, sd42_8_mss;

  SD42 sd42_1 (
    .saida(out_3[3:0]), .ms(sd42_2_mss), .ls(sd42_2_lss), .sel(in_1), .entrada(in_2[3:0]));  // open: mss, lss
  SD42 sd42_2 (
    .saida(out_3[7:4]), .mss(sd42_2_mss), .lss(sd42_2_lss), .ms(sd42_3_mss), .ls(sd42_3_lss), .sel(in_1),
    .entrada(in_2[7:4]));
  SD42 sd42_3 (
    .saida(out_3[11:8]), .mss(sd42_3_mss), .lss(sd42_3_lss), .ms(sd42_4_mss), .ls(sd42_4_lss), .sel(in_1),
    .entrada(in_2[11:8]));
  SD42 sd42_4 (
    .saida(out_3[15:12]), .mss(sd42_4_mss), .lss(sd42_4_lss), .ms(sd42_5_mss), .ls(sd42_5_lss), .sel(in_1),
    .entrada(in_2[15:12]));
  SD42 sd42_5 (
    .saida(out_3[19:16]), .mss(sd42_5_mss), .lss(sd42_5_lss), .ms(sd42_6_mss), .ls(sd42_6_lss), .sel(in_1),
    .entrada(in_2[19:16]));
  SD42 sd42_6 (
    .saida(out_3[23:20]), .mss(sd42_6_mss), .lss(sd42_6_lss), .ms(sd42_7_mss), .ls(sd42_7_lss), .sel(in_1),
    .entrada(in_2[23:20]));
  SD42 sd42_7 (
    .saida(out_3[27:24]), .mss(sd42_7_mss), .lss(sd42_7_lss), .ms(sd42_8_mss), .ls(sd42_8_lss), .sel(in_1),
    .entrada(in_2[27:24]));
  SD42 sd42_8 (
    .saida(out_3[31:28]), .mss(sd42_8_mss), .lss(sd42_8_lss), .ms(1'b0), .ls(1'b0), .sel(in_1),
    .entrada(in_2[31:28]));
endmodule

module SD84 (
  input  [7:0] entrada,
  input  e1,
  input  e2,
  input  e3,
  input  e4,
  input  sel,
  output s1,
  output s2,
  output s3,
  output s4,
  output [7:0] out_11
);

  Multiplexer multiplexer_1 (.in0(entrada[7]), .in1(e1), .out(out_11[7]), .sel(sel));
  Multiplexer multiplexer_2 (.in0(entrada[6]), .in1(e2), .out(out_11[6]), .sel(sel));
  Multiplexer multiplexer_3 (.in0(entrada[5]), .in1(e3), .out(out_11[5]), .sel(sel));
  Multiplexer multiplexer_4 (.in0(entrada[4]), .in1(e4), .out(out_11[4]), .sel(sel));
  Multiplexer multiplexer_5 (.in0(entrada[3]), .in1(entrada[7]), .out(out_11[3]), .sel(sel));
  Multiplexer multiplexer_6 (.in0(entrada[2]), .in1(entrada[6]), .out(out_11[2]), .sel(sel));
  Multiplexer multiplexer_7 (.in0(entrada[1]), .in1(entrada[5]), .out(out_11[1]), .sel(sel));
  Multiplexer multiplexer_8 (.in0(entrada[0]), .in1(entrada[4]), .out(out_11[0]), .sel(sel));

  assign s1 = entrada[3];
  assign s2 = entrada[2];
  assign s3 = entrada[1];
  assign s4 = entrada[0];
endmodule

module ShiftDIR4 (
  input  sel,
  input  [31:0] inn,
  output [31:0] out_3
);

  wire sd84_2_s1, sd84_2_s2, sd84_2_s3, sd84_2_s4, sd84_3_s1, sd84_3_s2, sd84_3_s3, sd84_3_s4, sd84_4_s1,
       sd84_4_s2, sd84_4_s3, sd84_4_s4;

  SD84 sd84_1 (
    .out_11(out_3[7:0]), .e1(sd84_2_s1), .e2(sd84_2_s2), .e3(sd84_2_s3), .e4(sd84_2_s4), .sel(sel),
    .entrada(inn[7:0]));  // open: s3, s4, s1, s2
  SD84 sd84_2 (
    .s3(sd84_2_s3), .s4(sd84_2_s4), .out_11(out_3[15:8]), .s1(sd84_2_s1), .s2(sd84_2_s2), .e1(sd84_3_s1),
    .e2(sd84_3_s2), .e3(sd84_3_s3), .e4(sd84_3_s4), .sel(sel), .entrada(inn[15:8]));
  SD84 sd84_3 (
    .s3(sd84_3_s3), .s4(sd84_3_s4), .out_11(out_3[23:16]), .s1(sd84_3_s1), .s2(sd84_3_s2), .e1(sd84_4_s1),
    .e2(sd84_4_s2), .e3(sd84_4_s3), .e4(sd84_4_s4), .sel(sel), .entrada(inn[23:16]));
  SD84 sd84_4 (
    .s3(sd84_4_s3), .s4(sd84_4_s4), .out_11(out_3[31:24]), .s1(sd84_4_s1), .s2(sd84_4_s2), .e1(1'b0),
    .e2(1'b0), .e3(1'b0), .e4(1'b0), .sel(sel), .entrada(inn[31:24]));
endmodule

module SD168 (
  input  [15:0] entrada,
  input  e1,
  input  e2,
  input  e3,
  input  e4,
  input  e5,
  input  e6,
  input  e7,
  input  e8,
  input  sel,
  output s1,
  output s2,
  output s3,
  output s4,
  output s5,
  output s6,
  output s7,
  output s8,
  output [15:0] saida
);

  Multiplexer multiplexer_1 (.in0(entrada[15]), .in1(e1), .out(saida[15]), .sel(sel));
  Multiplexer multiplexer_2 (.in0(entrada[14]), .in1(e2), .out(saida[14]), .sel(sel));
  Multiplexer multiplexer_3 (.in0(entrada[13]), .in1(e3), .out(saida[13]), .sel(sel));
  Multiplexer multiplexer_4 (.in0(entrada[12]), .in1(e4), .out(saida[12]), .sel(sel));
  Multiplexer multiplexer_5 (.in0(entrada[11]), .in1(e5), .out(saida[11]), .sel(sel));
  Multiplexer multiplexer_6 (.in0(entrada[10]), .in1(e6), .out(saida[10]), .sel(sel));
  Multiplexer multiplexer_7 (.in0(entrada[9]), .in1(e7), .out(saida[9]), .sel(sel));
  Multiplexer multiplexer_8 (.in0(entrada[8]), .in1(e8), .out(saida[8]), .sel(sel));
  Multiplexer multiplexer_9 (.in0(entrada[7]), .in1(entrada[15]), .out(saida[7]), .sel(sel));
  Multiplexer multiplexer_10 (.in0(entrada[6]), .in1(entrada[14]), .out(saida[6]), .sel(sel));
  Multiplexer multiplexer_11 (.in0(entrada[5]), .in1(entrada[13]), .out(saida[5]), .sel(sel));
  Multiplexer multiplexer_12 (.in0(entrada[4]), .in1(entrada[12]), .out(saida[4]), .sel(sel));
  Multiplexer multiplexer_13 (.in0(entrada[3]), .in1(entrada[11]), .out(saida[3]), .sel(sel));
  Multiplexer multiplexer_14 (.in0(entrada[2]), .in1(entrada[10]), .out(saida[2]), .sel(sel));
  Multiplexer multiplexer_15 (.in0(entrada[1]), .in1(entrada[9]), .out(saida[1]), .sel(sel));
  Multiplexer multiplexer_16 (.in0(entrada[0]), .in1(entrada[8]), .out(saida[0]), .sel(sel));

  assign s1 = entrada[7];
  assign s2 = entrada[6];
  assign s3 = entrada[5];
  assign s4 = entrada[4];
  assign s5 = entrada[3];
  assign s6 = entrada[2];
  assign s7 = entrada[1];
  assign s8 = entrada[0];
endmodule

module ShiftDIR8 (
  input  sel,
  input  [31:0] inn,
  output [31:0] out_3
);

  wire sd168_2_s1, sd168_2_s2, sd168_2_s3, sd168_2_s4, sd168_2_s5, sd168_2_s6, sd168_2_s7, sd168_2_s8;

  SD168 sd168_1 (
    .saida(out_3[15:0]), .sel(sel), .entrada(inn[15:0]), .e1(sd168_2_s1), .e2(sd168_2_s2), .e3(sd168_2_s3),
    .e4(sd168_2_s4), .e5(sd168_2_s5), .e6(sd168_2_s6), .e7(sd168_2_s7), .e8(sd168_2_s8));  // open: s1, s2, s3, s4, s5, s6, s7, s8
  SD168 sd168_2 (
    .saida(out_3[31:16]), .s1(sd168_2_s1), .s2(sd168_2_s2), .s3(sd168_2_s3), .s4(sd168_2_s4),
    .s5(sd168_2_s5), .s6(sd168_2_s6), .s7(sd168_2_s7), .s8(sd168_2_s8), .sel(sel), .entrada(inn[31:16]),
    .e1(1'b0), .e2(1'b0), .e3(1'b0), .e4(1'b0), .e5(1'b0), .e6(1'b0), .e7(1'b0), .e8(1'b0));
endmodule

module ShiftDIR16 (
  input  sel,
  input  [31:0] inn,
  output [31:0] out_3
);

  wire [31:0] shiftdir8_1_out_3;

  ShiftDIR8 shiftdir8_1 (.out_3(shiftdir8_1_out_3), .inn(inn), .sel(sel));
  ShiftDIR8 shiftdir8_2 (.out_3(out_3), .inn(shiftdir8_1_out_3), .sel(sel));
endmodule

module Somador1bit (
  input  in_1,
  input  in_2,
  input  Cin,
  output R
);

  wire xor_1_out;

  xor xor_1 (xor_1_out, in_1, in_2);
  xor xor_2 (R, xor_1_out, Cin);
endmodule

module sistemaLA4bits (
  input  A2,
  input  A3,
  input  A4,
  input  B2,
  input  A1,
  input  B3,
  input  B4,
  input  B1,
  input  c,
  output C2,
  output C3,
  output C1,
  output C4
);

  wire and_1_out, and_2_out, and_3_out, and_4_out, and_5_out, and_6_out, and_7_out, and_8_out, or_2_out,
       or_4_out, or_6_out, or_8_out;

  or or_1 (C4, and_1_out, and_2_out);
  and and_1 (and_1_out, A4, B4);
  or or_2 (or_2_out, A4, B4);
  and and_2 (and_2_out, or_2_out, C3);
  or or_3 (C3, and_3_out, and_4_out);
  and and_3 (and_3_out, A3, B3);
  and and_4 (and_4_out, or_4_out, C2);
  or or_4 (or_4_out, A3, B3);
  or or_5 (C2, and_5_out, and_6_out);
  and and_5 (and_5_out, A2, B2);
  or or_6 (or_6_out, A2, B2);
  and and_6 (and_6_out, or_6_out, C1);
  or or_7 (C1, and_7_out, and_8_out);
  and and_7 (and_7_out, A1, B1);
  and and_8 (and_8_out, or_8_out, c);
  or or_8 (or_8_out, A1, B1);
endmodule

module LookAhead4bits (
  input  [3:0] A,
  input  [3:0] B,
  input  Cin,
  output Cout,
  output [3:0] out_5
);

  wire sistemala4bits_1_c1, sistemala4bits_1_c2, sistemala4bits_1_c3;

  Somador1bit somador1bit_1 (.R(out_5[3]), .in_1(B[3]), .in_2(A[3]), .Cin(sistemala4bits_1_c3));
  Somador1bit somador1bit_2 (.R(out_5[2]), .in_1(B[2]), .in_2(A[2]), .Cin(sistemala4bits_1_c2));
  sistemaLA4bits sistemala4bits_1 (
    .C1(sistemala4bits_1_c1), .C4(Cout), .C3(sistemala4bits_1_c3), .C2(sistemala4bits_1_c2), .A2(A[1]),
    .B2(B[1]), .A1(A[0]), .B1(B[0]), .c(Cin), .A4(A[3]), .B4(B[3]), .A3(A[2]), .B3(B[2]));
  Somador1bit somador1bit_3 (.R(out_5[1]), .in_1(B[1]), .in_2(A[1]), .Cin(sistemala4bits_1_c1));
  Somador1bit somador1bit_4 (.R(out_5[0]), .in_1(B[0]), .in_2(A[0]), .Cin(Cin));
endmodule

module LAcomCS4bits (
  input  [3:0] A,
  input  [3:0] B,
  input  Csel,
  output [3:0] R,
  output Cout
);

  wire lookahead4bits_1_cout, lookahead4bits_2_cout;
  wire [3:0] lookahead4bits_1_out_5, lookahead4bits_2_out_5;

  Multiplexer multiplexer_1 (.in0(lookahead4bits_1_cout), .in1(lookahead4bits_2_cout), .out(Cout), .sel(Csel));
  LookAhead4bits lookahead4bits_1 (
    .Cout(lookahead4bits_1_cout), .out_5(lookahead4bits_1_out_5), .B(B), .A(A), .Cin(1'b0));
  Multiplexer #(.width(4)) multiplexer_2 (
    .in0(lookahead4bits_1_out_5), .in1(lookahead4bits_2_out_5), .out(R), .sel(Csel));
  LookAhead4bits lookahead4bits_2 (
    .Cout(lookahead4bits_2_cout), .out_5(lookahead4bits_2_out_5), .B(B), .A(A), .Cin(1'b1));
endmodule
